# Fritzing sketch Untitled Sketch 2 (saved by Fritzing 0.9.3b)
breadboards: 1

parts:
  S1 = Pushbutton [package="[THT]"]
  S2 = Pushbutton [package="[THT]"]
  IC1 = IC, DIP package, 28 pins [chip_label=ATmega328P]
  IC2 = IC, DIP package, 18 pins [chip_label=ULN2803]
  C2 = Ceramic Capacitor [capacitance=100nF package="100 mil [THT, multilayer]"]
  R1 = Resistor [tolerance=±5% resistance=10k package=THT]
  JACK1 = 2.1mm Barrel Jack with Terminal Block  # not connected
  MOTOR1 = 28BYJ-48 Stepper Motor

nets:
  N1: S1.Pin_1, S1.Pin_2, IC1.pin2
  N2: S1.Pin_3, S1.Pin_4, S2.Pin_3, S2.Pin_4, IC1.pin8, IC2.pin9, C2.1
  N3: S2.Pin_1, S2.Pin_2, IC1.pin1, R1.Pin_0
  N4: IC1.pin7, IC2.pin10, C2.0, R1.Pin_1, MOTOR1.RED
  N5: IC1.pin15, IC2.pin4
  N6: IC1.pin16, IC2.pin3
  N7: IC1.pin17, IC2.pin2
  N8: IC1.pin18, IC2.pin1
  N9: IC2.pin15, MOTOR1.BLUE
  N10: IC2.pin16, MOTOR1.PINK
  N11: IC2.pin17, MOTOR1.ORANGE
  N12: IC2.pin18, MOTOR1.YELLOW

custom parts:
  28BYJ-48 Stepper Motor: 28BYJ-48 gear-reduction stepper motor (small)
